// Logisim project main.circ as structural Verilog: 1 circuit, main circuit main
module main (
);

  wire and_1_out, and_2_out, and_3_out, cdm_8_1_p3, cl, code, comparator_1_eq, comparator_2_eq,
       comparator_3_eq, data, mem, not_1_out, r_w, reset;
  wire [7:0] addr, bank_n, cdm_8_1_p7, cdm_8_1_p8, IO;

  Clock clock_1 (.out(cl));
  Button button_1 (.out(reset));
  Comparator comparator_1 (.a(addr), .b({8{1'b1}}), .eq(comparator_1_eq));  // open: gt, lt
  and and_1 (and_1_out, comparator_1_eq, data);
  Register register_1 (.D(IO), .en(and_1_out), .Q(bank_n), .clk(cl), .clr(reset));
  Decoder #(.disabled(0)) decoder_1 (.out0(code), .out1(data), .sel(cdm_8_1_p3), .en(mem));
  // CdM_8 cdm_8_1: pin names not known; wires that end beside it: cl, reset, cdm_8_1_p3, mem, r_w, addr, cdm_8_1_p7, cdm_8_1_p8
  assign IO = not_1_out ? cdm_8_1_p7 : 8'bz;  // Controlled_Buffer controlled_buffer_1
  not not_1 (not_1_out, r_w);
  assign cdm_8_1_p8 = r_w ? IO : 8'bz;  // Controlled_Buffer controlled_buffer_2
  and and_2 (and_2_out, code, comparator_2_eq);
  Comparator comparator_2 (.a(bank_n), .b({8{1'b0}}), .eq(comparator_2_eq));  // open: gt, lt
  and and_3 (and_3_out, code, comparator_3_eq);
  Comparator comparator_3 (.a(bank_n), .b(8'h1), .eq(comparator_3_eq));  // open: gt, lt
  RAM ram_1 (.addr(addr), .data(IO), .sel(data), .clk(cl), .ld(r_w), .clr(reset));
  ROM rom_1 (.addr(addr), .data(IO), .sel(and_2_out));
  ROM rom_2 (.addr(addr), .data(IO), .sel(and_3_out));

  // Notes on the sheet:
  //   contents of rom_1 (hex, n*v repeats v):
  //   d1 f0 cc f0 d1 d d2 0 d3 4 5 e4 12 ab 8e 89 ee a d0 0 d1 6 a4 d1 d a4 d0 1 d1 10 d2 6 a e4 29 a4 8a
  //   8c 8d ee 20 8c d2 6 a e4 35 a4 8a 8c 8d ee 2c ee f7 192*0 d1 ff d0 1 a4 ee 0 d4
  //   contents of rom_2 (hex, n*v repeats v):
  //   d1 f0 cc f0 d1 d d2 0 d3 4 5 e4 12 ab 8e 89 ee a d0 0 d1 6 a4 d1 d a4 d0 1 d1 10 d2 6 a e4 29 a4 8a
  //   8c 8d ee 20 8c d2 6 a e4 35 a4 8a 8c 8d ee 2c ee f7 192*0 d1 ff d0 1 a4 ee 0 d4
endmodule
